// Logisim project RegisterFileAndALU.circ as structural Verilog
module ALU (
  input  [31:0] A,
  input  [31:0] B,
  input  [2:0] op,
  output [31:0] Result
);

  wire [0:0] comparator_1_lt;
  wire [31:0] adder_1_out, and_1_out, not_1_out, not_2_out, or_1_out, subtractor_1_out, xor_1_out;

  Adder #(.width(32)) adder_1 (.a(A), .b(B), .out(adder_1_out));  // open: cin, cout
  Subtractor #(.width(32)) subtractor_1 (.a(A), .b(B), .out(subtractor_1_out));  // open: bin, bout
  Comparator #(.width(32)) comparator_1 (.a(A), .b(B), .lt(comparator_1_lt[0]));  // open: gt, eq
  assign and_1_out = A & B;  // AND_Gate and_1, 32 bits wide
  assign or_1_out = A | B;  // OR_Gate or_1, 32 bits wide
  assign not_1_out = ~A;  // NOT_Gate not_1, 32 bits wide
  assign not_2_out = ~B;  // NOT_Gate not_2, 32 bits wide
  assign xor_1_out = A ^ B;  // XOR_Gate xor_1, 32 bits wide
  Multiplexer #(.enable("false"), .select(3), .width(32)) multiplexer_1 (
    .in0(adder_1_out), .in1(subtractor_1_out), .in2({{31{1'b0}}, comparator_1_lt[0]}), .in3(and_1_out),
    .in4(or_1_out), .in5(not_1_out), .in6(not_2_out), .in7(xor_1_out), .out(Result), .sel(op));
endmodule

module RegisterFile (
  input  write,
  input  [4:0] write_reg_num,
  input  [31:0] write_data,
  input  clock,
  input  [4:0] rd_reg_num_1,
  input  [4:0] rd_reg_num_2,
  input  [4:0] disp_reg,
  input  reset,
  output [31:0] read_data_1,
  output [31:0] read_data_2,
  output [31:0] disp_data
);

  wire and_1_out, and_2_out, and_3_out, and_4_out, and_5_out, and_6_out, and_7_out, and_8_out, and_9_out,
       and_10_out, and_11_out, and_12_out, and_13_out, and_14_out, and_15_out, and_16_out, and_17_out,
       and_18_out, and_19_out, and_20_out, and_21_out, and_22_out, and_23_out, and_24_out, and_25_out,
       and_26_out, and_27_out, and_28_out, and_29_out, and_30_out, and_31_out, decoder_1_out1,
       decoder_1_out2, decoder_1_out3, decoder_1_out4, decoder_1_out5, decoder_1_out6, decoder_1_out7,
       decoder_1_out8, decoder_1_out9, decoder_1_out10, decoder_1_out11, decoder_1_out12, decoder_1_out13,
       decoder_1_out14, decoder_1_out15, decoder_1_out16, decoder_1_out17, decoder_1_out18, decoder_1_out19,
       decoder_1_out20, decoder_1_out21, decoder_1_out22, decoder_1_out23, decoder_1_out24, decoder_1_out25,
       decoder_1_out26, decoder_1_out27, decoder_1_out28, decoder_1_out29, decoder_1_out30, decoder_1_out31;
  wire [31:0] register_1_q, register_2_q, register_3_q, register_4_q, register_5_q, register_6_q,
       register_7_q, register_8_q, register_9_q, register_10_q, register_11_q, register_12_q, register_13_q,
       register_14_q, register_15_q, register_16_q, register_17_q, register_18_q, register_19_q,
       register_20_q, register_21_q, register_22_q, register_23_q, register_24_q, register_25_q,
       register_26_q, register_27_q, register_28_q, register_29_q, register_30_q, register_31_q;

  Decoder #(.select(5)) decoder_1 (
    .out1(decoder_1_out1), .out2(decoder_1_out2), .out3(decoder_1_out3), .out4(decoder_1_out4),
    .out5(decoder_1_out5), .out6(decoder_1_out6), .out7(decoder_1_out7), .out8(decoder_1_out8),
    .out9(decoder_1_out9), .out10(decoder_1_out10), .out11(decoder_1_out11), .out12(decoder_1_out12),
    .out13(decoder_1_out13), .out14(decoder_1_out14), .out15(decoder_1_out15), .out16(decoder_1_out16),
    .out17(decoder_1_out17), .out18(decoder_1_out18), .out19(decoder_1_out19), .out20(decoder_1_out20),
    .out21(decoder_1_out21), .out22(decoder_1_out22), .out23(decoder_1_out23), .out24(decoder_1_out24),
    .out25(decoder_1_out25), .out26(decoder_1_out26), .out27(decoder_1_out27), .out28(decoder_1_out28),
    .out29(decoder_1_out29), .out30(decoder_1_out30), .out31(decoder_1_out31), .sel(write_reg_num), .en(write));  // open: out0
  and and_1 (and_1_out, write, decoder_1_out1);
  and and_2 (and_2_out, write, decoder_1_out2);
  and and_3 (and_3_out, write, decoder_1_out3);
  and and_4 (and_4_out, write, decoder_1_out4);
  and and_5 (and_5_out, write, decoder_1_out5);
  and and_6 (and_6_out, write, decoder_1_out6);
  and and_7 (and_7_out, write, decoder_1_out7);
  and and_8 (and_8_out, write, decoder_1_out8);
  and and_9 (and_9_out, write, decoder_1_out9);
  and and_10 (and_10_out, write, decoder_1_out10);
  and and_11 (and_11_out, write, decoder_1_out11);
  and and_12 (and_12_out, write, decoder_1_out12);
  and and_13 (and_13_out, write, decoder_1_out13);
  and and_14 (and_14_out, write, decoder_1_out14);
  and and_15 (and_15_out, write, decoder_1_out15);
  and and_16 (and_16_out, write, decoder_1_out16);
  and and_17 (and_17_out, write, decoder_1_out17);
  and and_18 (and_18_out, write, decoder_1_out18);
  and and_19 (and_19_out, write, decoder_1_out19);
  and and_20 (and_20_out, write, decoder_1_out20);
  and and_21 (and_21_out, write, decoder_1_out21);
  and and_22 (and_22_out, write, decoder_1_out22);
  and and_23 (and_23_out, write, decoder_1_out23);
  and and_24 (and_24_out, write, decoder_1_out24);
  and and_25 (and_25_out, write, decoder_1_out25);
  and and_26 (and_26_out, write, decoder_1_out26);
  and and_27 (and_27_out, write, decoder_1_out27);
  and and_28 (and_28_out, write, decoder_1_out28);
  and and_29 (and_29_out, write, decoder_1_out29);
  and and_30 (and_30_out, write, decoder_1_out30);
  and and_31 (and_31_out, write, decoder_1_out31);
  Register #(.width(32)) register_1 (.D(write_data), .en(and_1_out), .clk(clock), .Q(register_1_q), .clr(reset));
  Register #(.width(32)) register_2 (.D(write_data), .en(and_2_out), .clk(clock), .Q(register_2_q), .clr(reset));
  Register #(.width(32)) register_3 (.D(write_data), .en(and_3_out), .clk(clock), .Q(register_3_q), .clr(reset));
  Register #(.width(32)) register_4 (.D(write_data), .en(and_4_out), .clk(clock), .Q(register_4_q), .clr(reset));
  Register #(.width(32)) register_5 (.D(write_data), .en(and_5_out), .clk(clock), .Q(register_5_q), .clr(reset));
  Register #(.width(32)) register_6 (.D(write_data), .en(and_6_out), .clk(clock), .Q(register_6_q), .clr(reset));
  Register #(.width(32)) register_7 (.D(write_data), .en(and_7_out), .clk(clock), .Q(register_7_q), .clr(reset));
  Register #(.width(32)) register_8 (.D(write_data), .en(and_8_out), .clk(clock), .Q(register_8_q), .clr(reset));
  Register #(.width(32)) register_9 (.D(write_data), .en(and_9_out), .clk(clock), .Q(register_9_q), .clr(reset));
  Register #(.width(32)) register_10 (.D(write_data), .en(and_10_out), .clk(clock), .Q(register_10_q), .clr(reset));
  Register #(.width(32)) register_11 (.D(write_data), .en(and_11_out), .clk(clock), .Q(register_11_q), .clr(reset));
  Register #(.width(32)) register_12 (.D(write_data), .en(and_12_out), .clk(clock), .Q(register_12_q), .clr(reset));
  Register #(.width(32)) register_13 (.D(write_data), .en(and_13_out), .clk(clock), .Q(register_13_q), .clr(reset));
  Register #(.width(32)) register_14 (.D(write_data), .en(and_14_out), .clk(clock), .Q(register_14_q), .clr(reset));
  Register #(.width(32)) register_15 (.D(write_data), .en(and_15_out), .clk(clock), .Q(register_15_q), .clr(reset));
  Register #(.width(32)) register_16 (.D(write_data), .en(and_16_out), .clk(clock), .Q(register_16_q), .clr(reset));
  Register #(.width(32)) register_17 (.D(write_data), .en(and_17_out), .clk(clock), .Q(register_17_q), .clr(reset));
  Register #(.width(32)) register_18 (.D(write_data), .en(and_18_out), .clk(clock), .Q(register_18_q), .clr(reset));
  Register #(.width(32)) register_19 (.D(write_data), .en(and_19_out), .clk(clock), .Q(register_19_q), .clr(reset));
  Register #(.width(32)) register_20 (.D(write_data), .en(and_20_out), .clk(clock), .Q(register_20_q), .clr(reset));
  Register #(.width(32)) register_21 (.D(write_data), .en(and_21_out), .clk(clock), .Q(register_21_q), .clr(reset));
  Register #(.width(32)) register_22 (.D(write_data), .en(and_22_out), .clk(clock), .Q(register_22_q), .clr(reset));
  Register #(.width(32)) register_23 (.D(write_data), .en(and_23_out), .clk(clock), .Q(register_23_q), .clr(reset));
  Register #(.width(32)) register_24 (.D(write_data), .en(and_24_out), .clk(clock), .Q(register_24_q), .clr(reset));
  Register #(.width(32)) register_25 (.D(write_data), .en(and_25_out), .clk(clock), .Q(register_25_q), .clr(reset));
  Register #(.width(32)) register_26 (.D(write_data), .en(and_26_out), .clk(clock), .Q(register_26_q), .clr(reset));
  Register #(.width(32)) register_27 (.D(write_data), .en(and_27_out), .clk(clock), .Q(register_27_q), .clr(reset));
  Register #(.width(32)) register_28 (.D(write_data), .en(and_28_out), .clk(clock), .Q(register_28_q), .clr(reset));
  Register #(.width(32)) register_29 (.D(write_data), .en(and_29_out), .clk(clock), .Q(register_29_q), .clr(reset));
  Register #(.width(32)) register_30 (.D(write_data), .en(and_30_out), .clk(clock), .Q(register_30_q), .clr(reset));
  Register #(.width(32)) register_31 (.D(write_data), .en(and_31_out), .clk(clock), .Q(register_31_q), .clr(reset));
  Multiplexer #(.enable("false"), .select(5), .width(32)) multiplexer_1 (
    .in0({32{1'b0}}), .in1(register_1_q), .in2(register_2_q), .in3(register_3_q), .in4(register_4_q),
    .in5(register_5_q), .in6(register_6_q), .in7(register_7_q), .in8(register_8_q), .in9(register_9_q),
    .in10(register_10_q), .in11(register_11_q), .in12(register_12_q), .in13(register_13_q),
    .in14(register_14_q), .in15(register_15_q), .in16(register_16_q), .in17(register_17_q),
    .in18(register_18_q), .in19(register_19_q), .in20(register_20_q), .in21(register_21_q),
    .in22(register_22_q), .in23(register_23_q), .in24(register_24_q), .in25(register_25_q),
    .in26(register_26_q), .in27(register_27_q), .in28(register_28_q), .in29(register_29_q),
    .in30(register_30_q), .in31(register_31_q), .out(read_data_1), .sel(rd_reg_num_1));
  Multiplexer #(.enable("false"), .select(5), .width(32)) multiplexer_2 (
    .in0({32{1'b0}}), .in1(register_1_q), .in2(register_2_q), .in3(register_3_q), .in4(register_4_q),
    .in5(register_5_q), .in6(register_6_q), .in7(register_7_q), .in8(register_8_q), .in9(register_9_q),
    .in10(register_10_q), .in11(register_11_q), .in12(register_12_q), .in13(register_13_q),
    .in14(register_14_q), .in15(register_15_q), .in16(register_16_q), .in17(register_17_q),
    .in18(register_18_q), .in19(register_19_q), .in20(register_20_q), .in21(register_21_q),
    .in22(register_22_q), .in23(register_23_q), .in24(register_24_q), .in25(register_25_q),
    .in26(register_26_q), .in27(register_27_q), .in28(register_28_q), .in29(register_29_q),
    .in30(register_30_q), .in31(register_31_q), .out(read_data_2), .sel(rd_reg_num_2));
  Multiplexer #(.enable("false"), .select(5), .width(32)) multiplexer_3 (
    .in0({32{1'b0}}), .in1(register_1_q), .in2(register_2_q), .in3(register_3_q), .in4(register_4_q),
    .in5(register_5_q), .in6(register_6_q), .in7(register_7_q), .in8(register_8_q), .in9(register_9_q),
    .in10(register_10_q), .in11(register_11_q), .in12(register_12_q), .in13(register_13_q),
    .in14(register_14_q), .in15(register_15_q), .in16(register_16_q), .in17(register_17_q),
    .in18(register_18_q), .in19(register_19_q), .in20(register_20_q), .in21(register_21_q),
    .in22(register_22_q), .in23(register_23_q), .in24(register_24_q), .in25(register_25_q),
    .in26(register_26_q), .in27(register_27_q), .in28(register_28_q), .in29(register_29_q),
    .in30(register_30_q), .in31(register_31_q), .out(disp_data), .sel(disp_reg));

  // Notes on the sheet:
  //   hard-coded 0 for register $0
endmodule
